# Fritzing sketch NFCPuzzleSchema (saved by Fritzing 0.9.3b)
breadboards: 1

parts:
  Part1 = Arduino Uno (Rev3) - ICSP
  Componente1 = RFID-RC522-v3
  Componente2 = RFID-RC522-v3
  Componente3 = RFID-RC522-v3
  J1 = 220v plug
  S1 = Magnetic Door Switch [package=reed_switch_plastic]
  KY-1 = Keyes Relay [package=THT]

nets:
  N1: Part1.A0, KY-1.signal
  N2: Part1.D12/MISO, Componente1.MISO, Componente2.MISO, Componente3.MISO
  N3: Part1.D13/SCK, Componente1.SCK, Componente2.SCK, Componente3.SCK
  N4: Part1.D1/TX, Componente1.SDA
  N5: Part1.D2, Componente3.SDA
  N6: Part1.D3_PWM, Componente2.SDA
  N7: Part1.D7, Componente1.RST, Componente2.RST, Componente3.RST
  3.3V: Part1.3V3, Componente1.3.3V, Componente2.3.3V, Componente3.3.3V
  N8: Part1.5V, KY-1.power
  GND: Part1.GND, Componente1.GND, Componente2.GND, Componente3.GND, KY-1.ground
  N9: J1.pin1, S1.1
  N10: J1.pin2, KY-1.C
  N11: S1.2, KY-1.NO

custom parts:
  RFID-RC522-v3: A simple China made RFID-RC522 Reader (6x4 cm); do check the pin labels, as this is a MFRC522 based clone.
  220v plug: Generic 220V AC plug.
  Keyes Relay: The Keyes 5V relay module is suitable for SCM development, home appliance control. It uses a 5V~12V TIL control signal which can control DC / AC signal.
