# Fritzing sketch SwitchPuzzleSchema (saved by Fritzing 0.9.3b)
breadboards: 1

parts:
  Componente1 = Arduino Nano (Rev3.0)
  S1 = Toggle Switch [package=THT]
  S2 = Toggle Switch [package=THT]
  S3 = Toggle Switch [package=THT]
  S4 = Toggle Switch [package=THT]
  KY-1 = Keyes Relay [package=THT]
  S5 = Magnetic Door Switch [package=reed_switch_plastic]
  J1 = 220v plug
  S6 = Toggle Switch [package=THT]
  S7 = Toggle Switch [package=THT]
  S8 = Toggle Switch [package=THT]
  S9 = Toggle Switch [package=THT]

nets:
  N1: Componente1.GND, S1.L1, S2.L1, S3.L1, S4.L1, KY-1.ground, S6.L1, S7.L1, S8.L1, S9.L1
  N2: Componente1.D2, S9.L2
  N3: Componente1.D3, S8.L2
  N4: Componente1.D4, S6.L2
  N5: Componente1.D5, S4.L2
  N6: Componente1.D6, S3.L2
  N7: Componente1.D7, S2.L2
  N8: Componente1.D8, S1.L2
  N9: Componente1.D9, S7.L2
  N10: Componente1.5V, S1.COM, S2.COM, S3.COM, S4.COM, KY-1.power, S6.COM, S7.COM, S8.COM, S9.COM
  N11: Componente1.A1, KY-1.signal
  N12: KY-1.C, J1.pin2
  N13: KY-1.NO, S5.2
  N14: S5.1, J1.pin1

custom parts:
  Keyes Relay: The Keyes 5V relay module is suitable for SCM development, home appliance control. It uses a 5V~12V TIL control signal which can control DC / AC signal.
  220v plug: Generic 220V AC plug.
